# Fritzing sketch IntentDiagramRobotS3 (saved by Fritzing 1.0.5)

parts:
  C1 = Capacitor Polarized [package=cpol-radial-100uf-25v]
  ControladorIzquierdo = DRV8833 Motor Driver Board (MJKDZ) [package="DIP (Dual Inline) [THT]"]
  MotorIzquierdoTrasero = gear-motor
  C2 = Ceramic Capacitor [capacitance=100nF voltage=20V package="200 mil [THT, multilayer]"]
  MotorIzquierdoFrontal = gear-motor
  C3 = Ceramic Capacitor [capacitance=100nF voltage=20V package="200 mil [THT, multilayer]"]
  C4 = Capacitor Polarized [package=cpol-radial-100uf-25v]
  ControladorDerecho = DRV8833 Motor Driver Board (MJKDZ) [package="DIP (Dual Inline) [THT]"]
  MotorDerechoTrasero = gear-motor
  MotorDerechoFrontal = gear-motor
  C5 = Ceramic Capacitor [capacitance=100nF voltage=20V package="200 mil [THT, multilayer]"]
  C6 = Ceramic Capacitor [capacitance=100nF voltage=20V package="200 mil [THT, multilayer]"]
  EncoderIzqFrontalLm393 = CK-07 [package=THT]
  EncoderIzqInferiorLm394 = CK-07 [package=THT]
  EncoderDerFrontalLm395 = CK-07 [package=THT]
  EncoderDerInferiorLm396 = CK-07 [package=THT]
  Componente1 = TXB0108 8-channel Bi-directional Logic Level Converter
  A1 = ESP32-S3-WROOM-1-N16R8 dev board
  MPU6050 = InvenSense MPU6050
  7_7 = DC Power [voltage=7.7V internal_resistance=0.1Ω]
  V10 = DC Power [voltage=7.7 internal_resistance=0.1Ω]
  Switch_de_baterias_7_7V = Pushbutton [package=THT]
  part = Pushbutton [package=THT]
  PowerBank = DC Power [voltage=5V internal_resistance=0.1Ω]
  Switch_de_baterias_7_7V1 = Pushbutton [package=THT]

nets:
  N1: C1.-, ControladorIzquierdo.pin3
  N2: ControladorIzquierdo.pin1, A1.Pin_6
  N3: ControladorIzquierdo.pin2, A1.Pin_7
  N4: ControladorIzquierdo.pin5, A1.Pin_5
  N5: ControladorIzquierdo.pin6, A1.Pin_4
  N6: ControladorIzquierdo.pin8, MotorIzquierdoFrontal.pin_2
  N7: ControladorIzquierdo.pin9, MotorIzquierdoFrontal.pin_1, C3.1
  N8: ControladorIzquierdo.pin10, MotorIzquierdoTrasero.pin_2, C2.0
  N9: ControladorIzquierdo.pin11, MotorIzquierdoTrasero.pin_1, C2.1
  N10: C4.+, ControladorDerecho.pin4
  GND: C4.-, ControladorDerecho.pin3, EncoderIzqFrontalLm393.pin_3, EncoderIzqInferiorLm394.pin_3, EncoderDerFrontalLm395.pin_3, EncoderDerInferiorLm396.pin_3, Componente1.GND, PowerBank.V-
  N11: ControladorDerecho.pin1, A1.Pin_11
  N12: ControladorDerecho.pin2, A1.Pin_10
  N13: ControladorDerecho.pin5, A1.Pin_9
  N14: ControladorDerecho.pin6, A1.Pin_8
  N15: ControladorDerecho.pin8, MotorDerechoFrontal.pin_2
  N16: ControladorDerecho.pin9, MotorDerechoFrontal.pin_1, C6.1
  N17: ControladorDerecho.pin10, MotorDerechoTrasero.pin_2, C5.0
  N18: ControladorDerecho.pin11, MotorDerechoTrasero.pin_1, C5.1
  N19: EncoderIzqFrontalLm393.pin_2, Componente1.B5
  5V: EncoderIzqFrontalLm393.pin_4, EncoderIzqInferiorLm394.pin_4, EncoderDerFrontalLm395.pin_4, EncoderDerInferiorLm396.pin_4, Componente1.VCCB, Componente1.B8, A1.Pin_21
  N20: EncoderIzqInferiorLm394.pin_2, Componente1.B6
  N21: EncoderDerFrontalLm395.pin_2, Componente1.B2
  N22: EncoderDerInferiorLm396.pin_2, Componente1.B1
  N23: Componente1.OE, A1.Pin_41
  N24: Componente1.A6, A1.Pin_16
  N25: Componente1.A5, A1.Pin_17
  N26: Componente1.A2, A1.Pin_18
  N27: Componente1.A1, A1.Pin_19
  3.3V: Componente1.VCCA
  N28: A1.Pin_1, MPU6050.VCC
  N29: A1.Pin_12, MPU6050.SDA
  N30: A1.Pin_15, MPU6050.SCL
  N31: A1.Pin_23, A1.Pin_44, MPU6050.GND
  N32: 7_7.V-, V10.V-, part.leg0
  N33: 7_7.V+, V10.V+, Switch_de_baterias_7_7V.leg0
  N34: PowerBank.V+, Switch_de_baterias_7_7V1.leg0

notes:
  Zona de Potencia
  Zona de Encoders
  Fuentes de Poder
  Power Bank 5V
  2 baterias de 7V en paralelo
  3.3v se obtiene de ESP32

custom parts:
  DRV8833 Motor Driver Board (MJKDZ): A module made by MJKDZ, containg DRV8833 motor driver chip on PCB with 12-pin DIP 600mil footprint. Contains decoupling caps and an enable pad (J2). Does not bring out all IC pins. EEP = SLEEP input (needs pulling logic high to enable motors) ULT = FAULT output.
  CK-07: Fc-51 Infrared Obstacle Avoidance Proximity Sensor module. IR transmitter led, receiver LED, lm393 compaitor and a pot. 3.3 V to 5V power.
  TXB0108 8-channel Bi-directional Logic Level Converter: Because the Arduino (and Basic Stamp) are 5V devices, and most modern sensors, displays, flash cards and modes are 3.3V-only, many makers find that they need to perform level shifting/conversion to protect the 3.3V device from 5V. Although one can use resistors to make a divider, for high speed transfers, the resistors can add a lot of slew and cause havoc that is tough to debug. For that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
  ESP32-S3-WROOM-1-N16R8 dev board: ESP32-S3 WIFI+BLE5.0 Development Board ESP32-S3-WROOM-1-N16R8(16M Flash/8SRAM).
